# Fritzing sketch architecture doc fritzing (saved by Fritzing 0.9.3b)

parts:
  Arduino_Nano = Arduino Nano (Rev3.0)
  Servo_SG90_1 = Basic Servo
  Servo_SG90_2 = Basic Servo
  Power_Supply = Battery block 9V
  IR_Sensor_1 = fc-51 [package=THT]
  IR_Sensor_2 = fc-51 [package=THT]
  LED2 = smd LED [color="Red (633nm)" package="0805 [SMD]"]
  LED3 = smd LED [color="Yellow (595nm)" package="0805 [SMD]"]
  R2 = Resistor [tolerance=±5% resistance=220 package="2010 [SMD]"]
  LED1 = smd LED [color="Red (633nm)" package="0805 [SMD]"]
  LED4 = smd LED [color="Yellow (595nm)" package="0805 [SMD]"]
  R1 = Resistor [tolerance=±5% resistance=220 package="2010 [SMD]"]
  S1 = Toggle Switch [package=THT]

nets:
  GND: Arduino_Nano.GND, Servo_SG90_1.gnd, Servo_SG90_2.gnd, Power_Supply.-, IR_Sensor_1.pin2, IR_Sensor_2.pin2, LED2.cathode, LED3.cathode, LED1.cathode, LED4.cathode
  N1: Arduino_Nano.D4, R2.Pin_0
  N2: Arduino_Nano.D5, R1.Pin_0
  N3: Arduino_Nano.D8, IR_Sensor_2.pin1
  N4: Arduino_Nano.D9, IR_Sensor_1.pin1
  N5: Arduino_Nano.D10, Servo_SG90_2.pulse
  N6: Arduino_Nano.D11/MOSI, Servo_SG90_1.pulse
  N7: Arduino_Nano.VIN, S1.L2
  VCC: Arduino_Nano.5V, Servo_SG90_1.vcc, Servo_SG90_2.vcc, IR_Sensor_1.pin3, IR_Sensor_2.pin3
  N8: Power_Supply.+, S1.COM
  N9: LED2.anode, LED1.anode, R1.Pin_1
  N10: LED3.anode, R2.Pin_1, LED4.anode
